# Fritzing sketch PocketArcade (saved by Fritzing 0.9.3b)
breadboards: 1

parts:
  Part1 = TFT 2.8 inch 320x240 Touch w microSD [part_number=1770]
  PocketBeagle1 = PocketBeagle
  S1 = Pushbutton [package="[THT]"]
  S2 = Pushbutton [package="[THT]"]
  S3 = Pushbutton [package="[THT]"]
  S4 = Pushbutton [package="[THT]"]
  S5 = Pushbutton [package="[THT]"]
  S6 = Pushbutton [package="[THT]"]
  S7 = Pushbutton [package="[THT]"]
  S8 = Pushbutton [package="[THT]"]
  S9 = Pushbutton [package="[THT]"]
  S10 = Pushbutton [package="[THT]"]
  R1 = Resistor [tolerance=±5% resistance=470 package=THT]
  R2 = Resistor [tolerance=±5% resistance=470 package=THT]

nets:
  N1: Part1.+5V, PocketBeagle1.VOUT
  GND: Part1.GND, PocketBeagle1.GND, S1.Pin_1, S1.Pin_2, S2.Pin_1, S2.Pin_2, S3.Pin_1, S3.Pin_2, S4.Pin_1, S4.Pin_2, S6.Pin_1, S6.Pin_2, S7.Pin_1, S7.Pin_2, S9.Pin_1, S9.Pin_2, S10.Pin_2
  N2: Part1.SCLK, PocketBeagle1.SPI0.CLK
  N3: Part1.MISO, PocketBeagle1.SPI0.MISO
  N4: Part1.MOSI, PocketBeagle1.SPI0.MOSI
  N5: Part1.LCD_CS, PocketBeagle1.SPI0.CS
  N6: Part1.LCD_DC, PocketBeagle1.GPIO65
  N7: Part1.LCD_RST, PocketBeagle1.GPIO27
  N8: Part1.LCD_LITE, PocketBeagle1.PWM1A
  N9: PocketBeagle1.AIN6/GPIO87, S7.Pin_4
  N10: PocketBeagle1.GPIO26, S8.Pin_4
  N11: PocketBeagle1.GPIO59, S4.Pin_3, S4.Pin_4, R2.Pin_1
  N12: PocketBeagle1.GPIO58, S3.Pin_4
  N13: PocketBeagle1.GPIO57, S2.Pin_3, S2.Pin_4, R1.Pin_1
  N14: PocketBeagle1.GPIO60, S1.Pin_4
  N15: PocketBeagle1.GPIO64, S10.Pin_3, S10.Pin_4
  N16: PocketBeagle1.3.3V, R1.Pin_0, R2.Pin_0
  N17: PocketBeagle1.GPIO48, S9.Pin_3, S9.Pin_4
  N18: PocketBeagle1.GPIO45, S6.Pin_3, S6.Pin_4
  N19: PocketBeagle1.AIN5/GPIO86, S5.Pin_3, S5.Pin_4

custom parts:
  TFT 2.8 inch 320x240 Touch w microSD: This TFT display is big (2.8" diagonal) bright (4 white-LED backlight) and colorful! 240x320 pixels with individual RGB pixel control. As a bonus, this display has a resistive touchscreen attached to it already, so you can detect finger presses anywhere on the screen.
